# Fritzing sketch diagram-fritzing (saved by Fritzing 0.9.6b)
circuit board: 8.46667cm x 5.64444cm
breadboards: 1

parts:
  R6 = Resistor [tolerance=±20% power=0.25 resistance=10k package=THT]
  Microctrl = attiny85 [part_number=ATtiny85 package=dip]
  Thermistor = Temperature Sensor (Thermistor) [part_number="5k @ 25C" package=THT]
  Current_sensor = ACS712 [part_number=ACS712-20A package=so08]
  Triac = TRIAC [part_number=BT138 package=to-92]
  AC-DC_5V = DC_DC_XL4016 [part_number="ZK N7100-2A" package=board_screw]
  Optocoupler = MOC3031-M [part_number=TLP3022 package=dil06]
  Mains_&_Motor = AC Power [voltage=230V frequency=60 part_number="230VAC 50Hz"]
  M1 = DC Motor
  R2 = Resistor [tolerance=±20% power=0.25 resistance=330 package=THT]
  R3 = Resistor [tolerance=±20% power=0.25 resistance=150 package=THT]
  C1 = Ceramic Capacitor [capacitance=1µF voltage=35V package="100 mil [THT, multilayer]"]
  LED1 = LED - 5mm [color="Red (633nm)" current=0.030 package="5 mm [THT]"]
  R4 = Resistor [tolerance=±20% power=0.25 resistance=330 package=THT]
  Pot = Trimmer Potentiometer [maximum_resistance=50kΩ package=THT]
  33uF = Capacitor Polarized [package=panasonic_g]
  R7 = Resistor [tolerance=±20% power=0.25 resistance=100 package=THT]
  C2 = Ceramic Capacitor [capacitance=10nF voltage=35V package="100 mil [THT, multilayer]"]

nets:
  N1: R6.Pin_0, Microctrl.Pin_3, Thermistor.pin_0
  N2: R6.Pin_1, Microctrl.Pin_4, Current_sensor.GND, AC-DC_5V.OUT-, Optocoupler.2, C1.0, R4.Pin_1, Pot.leg2, 33uF.-
  N3: Microctrl.Pin_2, Pot.wiper
  N4: Microctrl.Pin_5, LED1.anode
  N5: Microctrl.Pin_6, R3.Pin_0
  N6: Microctrl.Pin_7, Current_sensor.VOUT
  N7: Microctrl.Pin_8, Thermistor.pin_1, Current_sensor.VCC, AC-DC_5V.OUT+, Pot.leg1, 33uF.+
  N8: Current_sensor.IP+, M1.pin_1
  N9: Current_sensor.IP-, Triac.M1, R7.Pin_1
  N10: Current_sensor.FILT, C1.1
  N11: Triac.G, Optocoupler.4
  N12: Triac.M2, AC-DC_5V.IN+, Mains_&_Motor.V+, R2.Pin_0, C2.0
  N13: AC-DC_5V.IN-, Mains_&_Motor.V-, M1.pin_2
  N14: Optocoupler.1, R3.Pin_1
  N15: Optocoupler.6, R2.Pin_1
  N16: LED1.cathode, R4.Pin_0
  N17: R7.Pin_0, C2.1

custom parts:
  Temperature Sensor (Thermistor): A 10k NTC Thermistor (Temperature Sensor)
